# Fritzing sketch iobot_esp-12_schematic (saved by Fritzing 0.9.2b)

parts:
  Step-down_module_AMS1117_3_3V = Voltage Regulator - 3.3V [package="TO220 [THT]"]
  Reset = Pushbutton [package="[SMD]"]
  Program = Pushbutton [package="[SMD]"]
  R1 = Resistor [tolerance=±5% resistance=10k package=THT]
  R2 = Resistor [tolerance=±5% resistance=10k package=THT]
  R3 = Resistor [tolerance=±5% resistance=220 package=THT]
  R4 = Resistor [tolerance=±5% resistance=220 package=THT]
  USB_to_FTDI_(CP2102_or_FT232) = FTDI Basic Programmer
  Motor_Power = 4 x AAA Battery Mount [part_number="4.8 - 6V"]
  ESP-12_Power = 4 x AAA Battery Mount [part_number="4.8 - 9V"]
  Right_Arm = Basic Servo [part_number=SG90]
  Body = Basic Servo [part_number=SG90]
  Head = Basic Servo [part_number=SG90]
  Left_Arm = Basic Servo [part_number=SG90]
  ESP-12 = ESP8266-12 WiFi Module [part_number=ESP8266]
  Left_LED = LED - 5mm [color="Red (633nm)" package="5 mm [THT]"]
  Right_LED = LED - 5mm [color="Red (633nm)" package="5 mm [THT]"]
  C1 = Ceramic Capacitor [capacitance=100nF package="100 mil [THT, multilayer]"]

nets:
  N1: Step-down_module_AMS1117_3_3V.input_voltage, ESP-12_Power.+
  GND: Step-down_module_AMS1117_3_3V.GND, Reset.Pin_1, Reset.Pin_2, Program.Pin_1, Program.Pin_2, USB_to_FTDI_(CP2102_or_FT232).GND, Motor_Power.-, ESP-12_Power.-, Right_Arm.gnd, Body.gnd, Head.gnd, Left_Arm.gnd, ESP-12.GND, Left_LED.cathode, Right_LED.cathode, C1.0
  N2: Step-down_module_AMS1117_3_3V.output_voltage, R1.Pin_0, R2.Pin_1, ESP-12.VCC, C1.1
  N3: Reset.Pin_3, Reset.Pin_4, R1.Pin_1, ESP-12.RESET
  N4: Program.Pin_3, Program.Pin_4, ESP-12.GPIO_0
  N5: R2.Pin_0, ESP-12.CH_PD
  N6: R3.Pin_0, ESP-12.GPIO_4
  N7: R3.Pin_1, Left_LED.anode
  N8: R4.Pin_0, ESP-12.GPIO_5
  N9: R4.Pin_1, Right_LED.anode
  N10: USB_to_FTDI_(CP2102_or_FT232).RXI, ESP-12.TXD
  N11: USB_to_FTDI_(CP2102_or_FT232).TXO, ESP-12.RXD
  VCC: Motor_Power.+, Right_Arm.vcc, Body.vcc, Head.vcc, Left_Arm.vcc
  N12: Right_Arm.pulse, ESP-12.GPIO_13
  N13: Body.pulse, ESP-12.GPIO_14
  N14: Head.pulse, ESP-12.GPIO_12
  N15: Left_Arm.pulse, ESP-12.GPIO_16

notes:
  IoBot ESP-12, 1.0

custom parts:
  ESP8266-12 WiFi Module: Generic WiFi Module based on the ESP8266 with onboard PCB antenna and UART communications
